// Logisim project ALU.circ as structural Verilog: 7 circuits, main circuit main
// +/ -
module Add_Sub (
  input  control,
  input  [1:0] A,
  input  [1:0] B,
  output [1:0] OUTPUT,
  output carry
);

  wire adder_1_cout, xor_1_out, xor_2_out;

  xor xor_1 (xor_1_out, control, B[0]);
  xor xor_2 (xor_2_out, control, B[1]);
  Adder #(.width(1)) adder_1 (.a(A[0]), .b(xor_1_out), .out(OUTPUT[0]), .cin(control), .cout(adder_1_cout));
  Adder #(.width(1)) adder_2 (.a(A[1]), .b(xor_2_out), .out(OUTPUT[1]), .cin(adder_1_cout), .cout(carry));

  // Notes on the sheet:
  //   A0
  //   B0
  //   A1
  //   B1
endmodule

// OR
module bitwise_OR (
  input  [1:0] A,
  input  [1:0] B,
  output [1:0] out_3
);

  or or_1 (out_3[0], A[0], B[0]);
  or or_2 (out_3[1], A[1], B[1]);
endmodule

// AND
module bitwise_AND (
  input  [1:0] A,
  input  [1:0] B,
  output [1:0] out_3
);

  and and_1 (out_3[0], A[0], B[0]);
  and and_2 (out_3[1], A[1], B[1]);
endmodule

// ++/--
module Increment_Decre (
  input  control,
  input  [1:0] A,
  input  _1,
  input  _1_2,
  output [1:0] \output ,
  output carry
);

  wire adder_1_cout, xor_1_out, xor_2_out;

  xor xor_1 (xor_1_out, control, _1);
  xor xor_2 (xor_2_out, control, _1_2);
  Adder #(.width(1)) adder_1 (.a(A[0]), .b(xor_1_out), .out(\output [0]), .cin(control), .cout(adder_1_cout));
  Adder #(.width(1)) adder_2 (.a(A[1]), .b(xor_2_out), .out(\output [1]), .cin(adder_1_cout), .cout(carry));
endmodule

// <<
module leftShifter (
  input  [1:0] A,
  input  shift,
  input  ZERO,
  output [1:0] \output 
);

  Multiplexer #(.enable("false")) multiplexer_1 (.in0(A[1]), .in1(A[0]), .out(\output [0]), .sel(shift));
  Multiplexer #(.disabled(0), .enable("false")) multiplexer_2 (.in0(A[0]), .in1(ZERO), .out(\output [1]), .sel(shift));
endmodule

module main (
  input  in_1,
  input  in_2,
  input  [2:0] in_3,
  input  [1:0] A,
  input  [1:0] B,
  output out_6,
  output [1:0] out_7
);

  wire and_1_out, not_1_out, not_2_out, undriven, undriven_2, undriven_3;

  not not_1 (not_1_out, in_3[1]);
  not not_2 (not_2_out, in_3[2]);
  and and_1 (and_1_out, in_3[0], not_1_out, not_2_out);
  Add_Sub add_sub_1 (.A(A), .B(B), .control(and_1_out), .OUTPUT(out_7), .carry(out_6));
  Increment_Decre increment_decre_1 (
    .A(A), ._1(in_1), ._1_2(in_1), .control(undriven_3), .\output (out_7), .carry(out_6));
  rshifter rshifter_1 (.ZERO(in_2), .A(A), .shift(undriven), .\output (out_7));
  leftShifter leftshifter_1 (.A(A), .ZERO(in_2), .\output (out_7), .shift(undriven_2));
  bitwise_AND bitwise_and_1 (.A(A), .B(B), .out_3(out_7));
  bitwise_OR bitwise_or_1 (.A(A), .B(B), .out_3(out_7));
endmodule

// >>
module rshifter (
  input  ZERO,
  input  [1:0] A,
  input  shift,
  output [1:0] \output 
);

  Multiplexer #(.enable("false")) multiplexer_1 (.in0(A[0]), .in1(ZERO), .out(\output [0]), .sel(shift));
  Multiplexer #(.disabled(0), .enable("false")) multiplexer_2 (.in0(A[1]), .in1(A[0]), .out(\output [1]), .sel(shift));
endmodule
